# Fritzing sketch SMARTO (saved by Fritzing 0.9.3b)
breadboards: 1

parts:
  U2 = ESP32S-HiLetgo [part_number=ESP32S-HiLetgo]
  1 = 2 Channel Power Relay
  Kamar_1 = Solenoid
  part = TTP223B Capacitive Touch Sensor Module [part_number="Kamar 1"]
  part_2 = TTP223B Capacitive Touch Sensor Module [part_number="Kamar 2"]
  Kamar_2 = Solenoid
  kamar_1 = smd LED [color="Red (633nm)" package="0603 [SMD]"]
  kamar_2 = smd LED [color="Red (633nm)" package="0603 [SMD]"]
  R1 = Resistor [tolerance=±5% resistance=220 package="2512 [SMD]"]
  R2 = Resistor [tolerance=±5% resistance=220 package="2512 [SMD]"]
  12V = 2.1mm Barrel Jack with Terminal Block

nets:
  VCC: U2.3.3, 1.VCC#14, part.VCC, part_2.VCC
  GND: U2.GND, 1.GND, part.GND, part_2.GND, kamar_1.anode, kamar_2.anode
  N1: U2.GPIO5, R1.Pin_1
  N2: U2.GPIO18, R2.Pin_1
  N3: U2.GPIO19, 1.IN2
  N4: U2.GPIO21, 1.IN1
  N5: U2.GPIO22, part_2.SIG
  N6: U2.GPIO23, part.SIG
  N7: 1.JD-VCC, 1.VCC#9
  N8: 1.K1-COM, 1.K2-COM, 12V.POS
  N9: Kamar_1.pin1, Kamar_2.pin1, 12V.NEG
  N10: kamar_1.cathode, R2.Pin_0
  N11: kamar_2.cathode, R1.Pin_0

custom parts:
  ESP32S-HiLetgo: HiLetgo ESP-WROOM-32 ESP32 ESP-32S Development Board 2.4GHz Dual-Mode WiFi + Bluetooth Dual Cores Microcontroller The ESP32 integrated with Antenna switches, RF Balun, power amplifiers, low-noise amplifiers, filters, and management modules, and the entire solution occupies the least area of PCB. 2.4 GHz Wi-Fi plus Bluetooth dual-mode chip, with TSMC Ultra-low power consumption 40nm technology,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
  2 Channel Power Relay: A 2 channel power relay. The module operates at 5V.
  TTP223B Capacitive Touch Sensor Module: The TTP223B capacitive touch sensor module uses the TTP223B IC. The appropriate voltage is approximately 2 to 5.5 volts.
